# Fritzing sketch PCB_Cube (saved by Fritzing 0.9.3b)
circuit board: 6.90183cm x 5.36183cm
breadboards: 1

parts:
  R1 = Resistor [tolerance=±5% resistance=100 package=THT]
  R2 = Resistor [tolerance=±5% resistance=100 package=THT]
  R3 = Resistor [tolerance=±5% resistance=100 package=THT]
  R4 = Resistor [tolerance=±5% resistance=100 package=THT]
  J3 = female pin header, 8 pins [form="♀ (female)"]
  J4 = female pin header, 10 pins [form="♀ (female)"]
  Arduino_Uno = Arduino Uno (Rev3) - ICSP
  J2 = female pin header, 4 pins [form="♀ (female)"]

nets:
  N1: R1.Pin_0, J2.pin4
  N2: R1.Pin_1, Arduino_Uno.A3
  N3: R2.Pin_0, J2.pin3
  N4: R2.Pin_1, Arduino_Uno.A2
  N5: R3.Pin_0, J2.pin2
  N6: R3.Pin_1, Arduino_Uno.A1
  N7: R4.Pin_0, J2.pin1
  N8: R4.Pin_1, Arduino_Uno.A0
  N9: J3.pin1, Arduino_Uno.D7
  N10: J3.pin2, Arduino_Uno.D6_PWM
  N11: J3.pin3, Arduino_Uno.D5_PWM
  N12: J3.pin4, Arduino_Uno.D4
  N13: J3.pin5, Arduino_Uno.D3_PWM
  N14: J3.pin6, Arduino_Uno.D2
  N15: J3.pin7, Arduino_Uno.D1/TX
  N16: J3.pin8, Arduino_Uno.D0/RX
  N17: J4.pin1, Arduino_Uno.A5/SCL
  N18: J4.pin2, Arduino_Uno.A4/SDA
  N19: J4.pin5, Arduino_Uno.D13/SCK
  N20: J4.pin6, Arduino_Uno.D12/MISO
  N21: J4.pin7, Arduino_Uno.D11_PWM/MOSI
  N22: J4.pin8, Arduino_Uno.D10_PWM/SS
  N23: J4.pin9, Arduino_Uno.D9_PWM
  N24: J4.pin10, Arduino_Uno.D8

notes:
  Cathodes
  Anodes
  Cubo de leds 4X4X4 , Mg. Fausto M. Lagos S. CC 4.0 BY-NC-SA , 2018 V1.0
  11
  12
  13
  14
  21
  22
  23
  24
  31
  32
  33
  34
  41
  42
  43
  44
  1
  2
  3
  4
