# Fritzing sketch HC_SR04_leds (saved by Fritzing 0.9.3b)
breadboards: 1

parts:
  hc-sr1 = hc-sr04
  R1 = Resistor [tolerance=±5% resistance=220 package=THT]
  R2 = Resistor [tolerance=±5% resistance=220 package=THT]
  R3 = Resistor [tolerance=±5% resistance=220 package=THT]
  R4 = Resistor [tolerance=±5% resistance=220 package=THT]
  R5 = Resistor [tolerance=±5% resistance=220 package=THT]
  LED1 = LED - 5mm [color="Blue (430nm)" package="5 mm [THT]"]
  LED2 = LED - 5mm [color="Green (555nm)" package="5 mm [THT]"]
  LED3 = LED - 5mm [color="Yellow (595nm)" package="5 mm [THT]"]
  LED4 = LED - 5mm [color="Orange (620nm)" package="5 mm [THT]"]
  LED5 = LED - 5mm [color="Red (633nm)" package="5 mm [THT]"]
  Componente1 = Arduino Uno (Rev3)

nets:
  VCC: hc-sr1.VCC, Componente1.5V
  N1: hc-sr1.Trig, Componente1.D3_PWM
  N2: hc-sr1.Echo, Componente1.D2
  GND: hc-sr1.GND, R1.Pin_0, R2.Pin_0, R3.Pin_0, R4.Pin_0, R5.Pin_0, Componente1.GND
  N3: R1.Pin_1, LED1.cathode
  N4: R2.Pin_1, LED2.cathode
  N5: R3.Pin_1, LED3.cathode
  N6: R4.Pin_1, LED4.cathode
  N7: R5.Pin_1, LED5.cathode
  N8: LED1.anode, Componente1.D9_PWM
  N9: LED2.anode, Componente1.D10_PWM/SS
  N10: LED3.anode, Componente1.D11_PWM/MOSI
  N11: LED4.anode, Componente1.D12/MISO
  N12: LED5.anode, Componente1.D13/SCK
